# Fritzing sketch adapter (saved by Fritzing 0.9.3b)
perfboards: 1

parts:
  J3 = female pin header, 4 pins [form="♀ (female)"]
  J4 = female pin header, 1 pin [form="♀ (female)"]  # not connected
  J5 = female pin header, 1 pin [form="♀ (female)"]
  U1 = attiny85 [package=dip]

nets:
  N1: J3.pin2, U1.Pin_2
  N2: J5.pin1, U1.Pin_3

notes:
  red: +5V
  black: GND
  green: DATA
  white: CLK
  5150 side
  PS/2 side
